# Fritzing sketch How to MQtt Series (saved by Fritzing 0.9.3b)
circuit board: 8.46667cm x 5.64444cm
breadboards: 1

parts:
  U1 = NodeMCU V1.0
  S1 = Pushbutton [package="[THT]"]
  R1 = Resistor [tolerance=±5% resistance=220 package=THT]
  LED1 = LED - 5mm [color="Red (633nm)" package="5 mm [THT]"]

nets:
  N1: U1.D0, S1.Pin_3, S1.Pin_4
  N2: U1.D1, R1.Pin_0
  N3: U1.GND, S1.Pin_1, S1.Pin_2, LED1.cathode
  N4: R1.Pin_1, LED1.anode

custom parts:
  NodeMCU V1.0: ESP8266 based NodeMCU

// code stored in the sketch: How to MQtt series.ino
#include <ESP8266WiFi.h>
#include <PubSubClient.h>
#define LED D0
const char* ssid = "Gearbox Staff";
const char* password =  "Staff@Gearbox";
const char* mqtt_server = "broker.hivemq.com";
const int mqtt_port = 1883;
WiFiClient espClient;
PubSubClient client(espClient);
void setup() 
{
  pinMode(LED, OUTPUT);
  pinMode(D1,INPUT_PULLUP);
  Serial.begin(9600);
  WiFi.begin(ssid, password);
  while (WiFi.status() != WL_CONNECTED) 
  {
    delay(500);
    Serial.println("Connecting to WiFi..");
  }
  Serial.print("Connected to WiFi :");
  Serial.println(WiFi.SSID());
  client.setServer(mqtt_server, mqtt_port);
  client.setCallback(MQTTcallback);
  while (!client.connected()) 
  {
    Serial.println("Connecting to MQTT...");
    if (client.connect("myTopic"))
    {
      Serial.println("connected");
    }
    else
    {
      Serial.print("failed with state ");
      Serial.println(client.state());
      delay(2000);
    }
  }
  client.subscribe("myTopic");
}
void MQTTcallback(char* topic, byte* payload, unsigned int length) 
{
  Serial.print("Message received in topic: ");
  Serial.println(topic);
  Serial.print("Message:");
  String message;
  for (int i = 0; i < length; i++) 
  {
    message = message + (char)payload[i];
  }
  Serial.print(message);
  if (message == "on") 
  {
    digitalWrite(LED, HIGH);
  }
  else if (message == "off") 
  {
    digitalWrite(LED, LOW);
  }
  Serial.println();
  Serial.println("-----------------------");
}
void loop() 
{
  if(digitalRead(D1)==0)
  {
  client.publish("myTopic", "Hello from ESP8266");
  delay(1000);
  }
  else;
  client.loop();
}
